# Fritzing sketch OpenFit (saved by Fritzing 0.7.5b)

parts:
  FubarinoSD2 = IC, DIP package, 56 pins [chip_label=FubarinoSD spacing=900mil]
  LCD1 = LCD screen
  R1 = Resistor [tolerance=±5% resistance=220 package=THT]
  R2 = Rotary Potentiometer (Small) [maximum_resistance=100kΩ]
  Part1 = IMU Digital Combo Board 6DOF  # not connected

nets:
  N1: FubarinoSD2.pin6, LCD1.DB7
  N2: FubarinoSD2.pin7, LCD1.DB6
  N3: FubarinoSD2.pin8, LCD1.DB5
  N4: FubarinoSD2.pin9, LCD1.DB4
  N5: FubarinoSD2.pin15, LCD1.E
  N6: FubarinoSD2.pin16, LCD1.RS
  GND: LCD1.VSS, LCD1.R/W, LCD1.LED-, R2.leg2
  5V: LCD1.VDD, R1.Pin_1, R2.leg1
  N7: LCD1.V0, R2.wiper
  N8: LCD1.LED+, R1.Pin_0
